# Fritzing sketch AutNavodnjavanje (saved by Fritzing 0.9.3b)
breadboards: 1

parts:
  Part1 = Arduino Nano (Rev3.0)  # not connected
  L1 = Solenoid
  D1 = Rectifier Diode [package="Melf DO-213 AA [SMD]"]
  WeMos_D1_Mini_Relay_Shield_V1 = WeMos D1 Mini Relay Shield V2  # not connected
  S1 = Tilt Switch [package=THT]  # not connected
  S2 = Tilt Switch [package=THT]  # not connected

nets:
  N1: L1.pin1, D1.anode
  N2: L1.pin2, D1.cathode
