# Fritzing sketch AutNavodnjavanje1 (saved by Fritzing 0.9.6b)
breadboards: 1

parts:
  L1 = Solenoid
  D1 = Rectifier Diode [package="Melf DO-213 AA [SMD]"]
  ZS-042_RTC1 = ZS-042 RTC Module
  KY-1 = Keyes Relay [package=THT]
  LCD1 = LCD screen
  Keypad4x1 = Keypad Membran 4x4
  Part2 = Arduino Uno (Rev3) - ICSP
  U1 = POT [package=pot_mammoth]

nets:
  N1: L1.pin1, D1.anode, KY-1.C
  N2: L1.pin2, D1.cathode, KY-1.NC
  GND: ZS-042_RTC1.GND, KY-1.ground, LCD1.VSS, LCD1.R/W, LCD1.LED-, Part2.GND, U1.S
  VCC: ZS-042_RTC1.VCC, KY-1.power, LCD1.VDD, LCD1.LED+, Part2.5V, U1.E
  N3: ZS-042_RTC1.SDA, Part2.A4/SDA
  N4: ZS-042_RTC1.SCL, Part2.A5/SCL
  N5: KY-1.signal, Part2.A3
  N6: LCD1.V0, U1.A
  N7: LCD1.RS, Part2.A2
  N8: LCD1.E, Part2.A1
  N9: LCD1.DB4, Part2.D10_PWM/SS
  N10: LCD1.DB5, Part2.D11_PWM/MOSI
  N11: LCD1.DB6, Part2.D12/MISO
  N12: LCD1.DB7, Part2.D13/SCK
  N13: Keypad4x1.Pin1, Part2.D9_PWM
  N14: Keypad4x1.Pin2, Part2.D8
  N15: Keypad4x1.Pin3, Part2.D7
  N16: Keypad4x1.Pin4, Part2.D6_PWM
  N17: Keypad4x1.Pin5, Part2.D5_PWM
  N18: Keypad4x1.Pin6, Part2.D4
  N19: Keypad4x1.Pin7, Part2.D3_PWM
  N20: Keypad4x1.Pin8, Part2.D2

notes:
  AUTOMATSKO NAVODNJAVANJE
  29/04/2021
  BORIS BLAGOEJVIĆ

custom parts:
  Keyes Relay: The Keyes 5V relay module is suitable for SCM development, home appliance control. It uses a 5V~12V TIL control signal which can control DC / AC signal.
  Keypad Membran 4x4: Membrane Keypad 4x4 Matrix
